// Logisim project 16BitCPU.circ as structural Verilog: 1 circuit, main circuit main
module main (
);

  wire A_IN, A_OUT, B_IN, B_OUT, CLK, counter_1_carry, PC_ENABLE, PC_IN, PC_OUT, PC_RESET,
       pull_resistor_1_node, pull_resistor_2_node, RAM_ENABLE, RAM_STORE;
  wire [7:0] counter_1_q, counter_2_q;
  wire [15:0] MAIN_BUS, ram_1_dout, register_1_q, register_2_q, register_3_q;

  Pull_Resistor pull_resistor_1 (.node(pull_resistor_1_node));
  Register #(.width(16)) register_1 (
    .D(MAIN_BUS), .en(pull_resistor_1_node), .Q(register_1_q), .clk(CLK), .clr(pull_resistor_2_node));
  Pull_Resistor pull_resistor_2 (.node(pull_resistor_2_node));
  RAM #(.addrWidth(16), .dataWidth(16)) ram_1 (
    .addr(register_1_q), .we(RAM_STORE), .oe(RAM_ENABLE), .clk(CLK), .dout(ram_1_dout));  // open: din
  assign MAIN_BUS = RAM_ENABLE ? ram_1_dout : 16'bz;  // Controlled_Buffer controlled_buffer_1
  LED led_1 (.in(MAIN_BUS[15]));
  LED led_2 (.in(MAIN_BUS[14]));
  LED led_3 (.in(MAIN_BUS[13]));
  LED led_4 (.in(MAIN_BUS[12]));
  LED led_5 (.in(MAIN_BUS[11]));
  LED led_6 (.in(MAIN_BUS[10]));
  Clock clock_1 (.out(CLK));
  LED led_7 (.in(MAIN_BUS[9]));
  LED led_8 (.in(MAIN_BUS[8]));
  LED led_9 (.in(MAIN_BUS[7]));
  LED led_10 (.in(MAIN_BUS[6]));
  LED led_11 (.in(MAIN_BUS[5]));
  LED led_12 (.in(MAIN_BUS[4]));
  LED led_13 (.in(MAIN_BUS[3]));
  LED led_14 (.in(MAIN_BUS[2]));
  Pull_Resistor pull_resistor_3 (.node(MAIN_BUS));
  LED led_15 (.in(MAIN_BUS[1]));
  LED led_16 (.in(MAIN_BUS[0]));
  Pull_Resistor pull_resistor_4 (.node(RAM_STORE));
  Pull_Resistor #(.pull(1)) pull_resistor_5 (.node(RAM_ENABLE));
  Pull_Resistor pull_resistor_6 (.node(PC_ENABLE));
  Pull_Resistor pull_resistor_7 (.node(PC_RESET));
  Pull_Resistor pull_resistor_8 (.node(PC_IN));
  Pull_Resistor pull_resistor_9 (.node(PC_OUT));
  Counter counter_1 (
    .load(PC_IN), .D(MAIN_BUS[7:0]), .count(PC_ENABLE), .Q(counter_1_q), .carry(counter_1_carry), .up(1'b1),
    .clk(CLK), .clr(PC_RESET));
  assign MAIN_BUS[7:0] = PC_OUT ? counter_1_q : 8'bz;  // Controlled_Buffer controlled_buffer_2
  assign MAIN_BUS[15:8] = PC_OUT ? counter_2_q : 8'bz;  // Controlled_Buffer controlled_buffer_3
  Pull_Resistor pull_resistor_10 (.node(A_OUT));
  Counter counter_2 (
    .load(PC_IN), .D(MAIN_BUS[15:8]), .count(counter_1_carry), .Q(counter_2_q), .up(1'b1), .clk(CLK),
    .clr(PC_RESET));  // open: carry
  Pull_Resistor pull_resistor_11 (.node(A_IN));
  Pull_Resistor pull_resistor_12 (.node(B_OUT));
  Pull_Resistor pull_resistor_13 (.node(B_IN));
  Register #(.width(16)) register_2 (.D(MAIN_BUS), .en(A_IN), .clk(CLK), .Q(register_2_q));  // open: clr
  Register #(.width(16)) register_3 (.D(MAIN_BUS), .en(B_IN), .clk(CLK), .Q(register_3_q));  // open: clr
  assign MAIN_BUS = A_OUT ? register_2_q : 16'bz;  // Controlled_Buffer controlled_buffer_4
  assign MAIN_BUS = B_OUT ? register_3_q : 16'bz;  // Controlled_Buffer controlled_buffer_5

  // Notes on the sheet:
  //   Program Counter - 16Bit
  //   Register A - 16Bit
  //   Register B - 16Bit
endmodule
